# Fritzing sketch First Circuit (saved by Fritzing 1.0.6)
breadboards: 1

parts:
  Mod1 = Raspberry Pi 4B
  R1 = Resistor [tolerance=±5% power=0.25W resistance=1K package=THT]
  LED1 = smd LED [color="Red (633nm)" package="0603 [SMD]"]

nets:
  N1: Mod1.GND, LED1.cathode
  N2: Mod1.GPIO17, R1.Pin_1
  N3: R1.Pin_0, LED1.anode
