# Fritzing sketch PIR Sensor (saved by Fritzing 1.0.6)
breadboards: 1

parts:
  Mod1 = Raspberry Pi 4B
  R1 = Resistor [tolerance=±5% power=0.25W resistance=1K package=THT]
  LED1 = smd LED [color="Red (633nm)" package="0603 [SMD]"]
  S1 = Pushbutton [package="[SMD]"]
  R2 = Resistor [tolerance=±5% resistance=1k package="1206 [SMD]"]
  LED2 = smd LED [color="Blue (430nm)" package="0603 [SMD]"]
  LED3 = smd LED [color="Green (555nm)" package="0603 [SMD]"]
  R3 = Resistor [tolerance=±5% power=0.25W resistance=1K package=THT]
  R4 = Resistor [tolerance=±5% power=0.25W resistance=1K package=THT]
  PIR1 = PIR sensor
  R5 = Resistor [tolerance=±5% resistance=1k package="1206 [SMD]"]

nets:
  5V: Mod1.5V, PIR1.VDD
  GND: Mod1.GND, LED1.cathode, S1.Pin_3, S1.Pin_4, LED2.cathode, LED3.cathode, PIR1.GND
  N1: Mod1.GPIO4, R5.Pin_1
  N2: Mod1.GPIO17, R1.Pin_1
  N3: Mod1.GPIO27, R3.Pin_1
  N4: Mod1.GPIO22, R4.Pin_1
  N5: Mod1.GPIO26, R2.Pin_1
  N6: R1.Pin_0, LED1.anode
  N7: S1.Pin_1, S1.Pin_2, R2.Pin_0
  N8: LED2.anode, R3.Pin_0
  N9: LED3.anode, R4.Pin_0
  N10: PIR1.SIG, R5.Pin_0
