# Fritzing sketch Push Button Circuit (saved by Fritzing 1.0.6)
breadboards: 1

parts:
  Mod1 = Raspberry Pi 4B
  R1 = Resistor [tolerance=±5% power=0.25W resistance=1K package=THT]
  LED1 = smd LED [color="Red (633nm)" package="0603 [SMD]"]
  S1 = Pushbutton [package="[SMD]"]
  R2 = Resistor [tolerance=±5% resistance=1k package="1206 [SMD]"]

nets:
  N1: Mod1.GND, LED1.cathode, S1.Pin_3, S1.Pin_4
  N2: Mod1.GPIO17, R1.Pin_1
  N3: Mod1.GPIO26, R2.Pin_1
  N4: R1.Pin_0, LED1.anode
  N5: S1.Pin_1, S1.Pin_2, R2.Pin_0
